# Fritzing sketch CUIDA-UPS (saved by Fritzing 0.9.5d)
breadboards: 1

parts:
  UPS1 = cuida_ups
  BATTERY1 = cuida_battery
  CAPACITOR1 = cuida_capacitor  # not connected
  MODEM1 = cuida_modem
  MPU1 = cuida_mpu6050
  ESP1 = cuida_esp32
  GPS1 = cuida_gps
  POWER1 = cuida_power

nets:
  N1: UPS1.connector0, POWER1.connector0
  N2: UPS1.connector1, POWER1.connector1
  N3: UPS1.connector4, BATTERY1.connector0
  N4: UPS1.connector5, BATTERY1.connector1
  N5: MODEM1.connector2, ESP1.connector23
  N6: MODEM1.connector3, ESP1.connector24
  N7: MPU1.connector2, ESP1.connector16
  N8: MPU1.connector3, ESP1.connector19
  N9: ESP1.connector8, GPS1.connector3
  N10: ESP1.connector9, GPS1.connector2
