# Fritzing sketch CUIDA-v0.1 (saved by Fritzing 1.0.0)
breadboards: 1

parts:
  ESP32_DevKit_V1_-_30_pin_wiring_model = ESP32 DevKit V1 - 30 pin wiring model
  MPU6050_breakout_-_used_pins = MPU6050 breakout - used pins
  GY-NEO6MV2_GPS_breakout_-_illustrative_header_order = GY-NEO6MV2 GPS breakout - illustrative header order
  A7670SA_carrier_-_simplified_used-pin_model = A7670SA carrier - simplified used-pin model
  Regulated_12V_car_adapter_-_5V_2A_output = Regulated 12V car adapter - 5V 2A output
  1000uF_polarized_capacitor_-_10V_minimum = 1000uF polarized capacitor - 10V minimum

nets:
  N1: ESP32_DevKit_V1_-_30_pin_wiring_model.26, GY-NEO6MV2_GPS_breakout_-_illustrative_header_order.RX
  N2: ESP32_DevKit_V1_-_30_pin_wiring_model.27, GY-NEO6MV2_GPS_breakout_-_illustrative_header_order.TX
  GND: ESP32_DevKit_V1_-_30_pin_wiring_model.GND_A, ESP32_DevKit_V1_-_30_pin_wiring_model.GND_B, MPU6050_breakout_-_used_pins.GND, MPU6050_breakout_-_used_pins.AD0, GY-NEO6MV2_GPS_breakout_-_illustrative_header_order.GND, A7670SA_carrier_-_simplified_used-pin_model.GND, Regulated_12V_car_adapter_-_5V_2A_output.GND, 1000uF_polarized_capacitor_-_10V_minimum.-
  VIN: ESP32_DevKit_V1_-_30_pin_wiring_model.VIN, GY-NEO6MV2_GPS_breakout_-_illustrative_header_order.VCC, A7670SA_carrier_-_simplified_used-pin_model.VIN, Regulated_12V_car_adapter_-_5V_2A_output.5V, 1000uF_polarized_capacitor_-_10V_minimum.+
  N3: ESP32_DevKit_V1_-_30_pin_wiring_model.22, MPU6050_breakout_-_used_pins.SCL
  N4: ESP32_DevKit_V1_-_30_pin_wiring_model.21, MPU6050_breakout_-_used_pins.SDA
  N5: ESP32_DevKit_V1_-_30_pin_wiring_model.17, A7670SA_carrier_-_simplified_used-pin_model.RXD
  N6: ESP32_DevKit_V1_-_30_pin_wiring_model.16, A7670SA_carrier_-_simplified_used-pin_model.TXD
  3V3: ESP32_DevKit_V1_-_30_pin_wiring_model.3V3, MPU6050_breakout_-_used_pins.VCC

custom parts:
  ESP32 DevKit V1 - 30 pin wiring model: Virtual prototype part. Mechanical dimensions and unused header positions are illustrative; not a fabrication footprint.
  MPU6050 breakout - used pins: Virtual prototype part. Mechanical dimensions and unused header positions are illustrative; not a fabrication footprint.
  GY-NEO6MV2 GPS breakout - illustrative header order: Virtual prototype part. Mechanical dimensions and unused header positions are illustrative; not a fabrication footprint.
  A7670SA carrier - simplified used-pin model: Virtual prototype part. Mechanical dimensions and unused header positions are illustrative; not a fabrication footprint.
  Regulated 12V car adapter - 5V 2A output: Virtual prototype part. Mechanical dimensions and unused header positions are illustrative; not a fabrication footprint.
  1000uF polarized capacitor - 10V minimum: Virtual prototype part. Mechanical dimensions and unused header positions are illustrative; not a fabrication footprint.
