# Fritzing sketch CUIDA (saved by Fritzing 0.9.5d)
breadboards: 1

parts:
  CAPACITOR1 = cuida_capacitor  # not connected
  MODEM1 = cuida_modem
  MPU1 = cuida_mpu6050
  ESP1 = cuida_esp32
  GPS1 = cuida_gps
  POWER1 = cuida_power  # not connected

nets:
  N1: MODEM1.connector2, ESP1.connector23
  N2: MODEM1.connector3, ESP1.connector24
  N3: MPU1.connector2, ESP1.connector16
  N4: MPU1.connector3, ESP1.connector19
  N5: ESP1.connector8, GPS1.connector3
  N6: ESP1.connector9, GPS1.connector2
